# Fritzing sketch Bike_Lock_Diagram (saved by Fritzing 0.9.3b)

parts:
  Part1 = sensor_biometrico
  Part2 = Arduino Uno (Rev3)
  LED1 = smd LED [color="Green (565nm)" package="1206 [SMD]"]
  LED2 = smd LED [color="Red (633nm)" package="1206 [SMD]"]
  Mod1 = KY-020 Tilt Switch Module [package="Breakout board"]
  Part3 = Bluetooth HC-05 Macho
  S1 = SWITCH-MOMENTARY-2 [package=tactile-pth-12mm]
  R1 = Resistor [tolerance=±5% resistance=220 package="0402 [SMD]"]
  Part4 = Passive Buzzer
  R2 = Resistor [tolerance=±5% resistance=220 package="0402 [SMD]"]
  R3 = Resistor [tolerance=±5% resistance=220 package="0402 [SMD]"]

nets:
  VCC: Part1.VCC, Part2.5V, Part4.S, R3.Pin_1
  GND: Part1.GND, Part2.GND, LED1.cathode, LED2.cathode, Mod1.-, Part4.GND
  N1: Part2.D0/RX, Part3.TXD
  N2: Part2.D1/TX, Part3.RXD
  N3: LED1.anode, R1.Pin_0
  N4: LED2.anode, R2.Pin_0
  N5: Part3.GND, S1.2
  N6: S1.1, R3.Pin_0

custom parts:
  sensor_biometrico: Adafruit Optical Fingerprint Sensor
  KY-020 Tilt Switch Module: KY-020 tilt switch sensor module. Closes the circuit when it is tilted to the side as long as it is moved with enough force and degree of inclination to activate the ball switch inside.
